// Logisim project one.circ as structural Verilog: 3 circuits, main circuit main
module main (
);

  _16regs u_16regs_1 ();  // open: CX0, LX0, X0, LX1, LX2, ck, reset, X1, X2
endmodule

module _4regs (
  input  esto,
  input  [15:0] datain,
  input  [1:0] select,
  input  control1,
  input  in_5,
  input  in_6,
  input  [1:0] A1,
  input  control2,
  input  [1:0] A2,
  output [15:0] out1,
  output [15:0] out2
);

  wire decoder_1_out0, decoder_1_out1, decoder_1_out2, decoder_1_out3, decoder_2_out0, decoder_2_out1,
       decoder_2_out2, decoder_2_out3, decoder_3_out0, decoder_3_out1, decoder_3_out2, decoder_3_out3;
  wire [15:0] register_1_q, register_2_q, register_3_q, register_4_q;

  Decoder #(.select(2), .disabled(0)) decoder_1 (
    .out0(decoder_1_out0), .out1(decoder_1_out1), .out2(decoder_1_out2), .out3(decoder_1_out3), .sel(select),
    .en(esto));
  Register #(.width(16)) register_1 (.D(datain), .en(decoder_1_out0), .Q(register_1_q), .clk(in_5), .clr(in_6));
  Register #(.width(16)) register_2 (.D(datain), .en(decoder_1_out1), .Q(register_2_q), .clk(in_5), .clr(in_6));
  Register #(.width(16)) register_3 (.D(datain), .en(decoder_1_out2), .Q(register_3_q), .clk(in_5), .clr(in_6));
  Register #(.width(16)) register_4 (.D(datain), .en(decoder_1_out3), .Q(register_4_q), .clk(in_5), .clr(in_6));
  Decoder #(.select(2), .disabled(0)) decoder_2 (
    .out0(decoder_2_out0), .out1(decoder_2_out1), .out2(decoder_2_out2), .out3(decoder_2_out3), .sel(A1),
    .en(control1));
  assign out1 = decoder_2_out0 ? register_1_q : 16'bz;  // Controlled_Buffer controlled_buffer_1
  assign out1 = decoder_2_out1 ? register_2_q : 16'bz;  // Controlled_Buffer controlled_buffer_2
  assign out1 = decoder_2_out2 ? register_3_q : 16'bz;  // Controlled_Buffer controlled_buffer_3
  assign out1 = decoder_2_out3 ? register_4_q : 16'bz;  // Controlled_Buffer controlled_buffer_4
  Decoder #(.select(2), .disabled(0)) decoder_3 (
    .out0(decoder_3_out0), .out1(decoder_3_out1), .out2(decoder_3_out2), .out3(decoder_3_out3), .sel(A2),
    .en(control2));
  assign out2 = decoder_3_out0 ? register_1_q : 16'bz;  // Controlled_Buffer controlled_buffer_5
  assign out2 = decoder_3_out1 ? register_2_q : 16'bz;  // Controlled_Buffer controlled_buffer_6
  assign out2 = decoder_3_out2 ? register_3_q : 16'bz;  // Controlled_Buffer controlled_buffer_7
  assign out2 = decoder_3_out3 ? register_4_q : 16'bz;  // Controlled_Buffer controlled_buffer_8
endmodule

module _16regs (
  input  CX0,
  input  [3:0] LX0,
  input  [15:0] X0,
  input  [3:0] LX1,
  input  ck,
  input  reset,
  input  [3:0] LX2,
  output [15:0] X1,
  output [15:0] X2
);

  wire decoder_1_out0, decoder_1_out1, decoder_1_out2, decoder_1_out3, decoder_2_out0, decoder_2_out1,
       decoder_2_out2, decoder_2_out3, decoder_3_out0, decoder_3_out1, decoder_3_out2, decoder_3_out3;

  Decoder #(.select(2), .disabled(0)) decoder_1 (
    .out0(decoder_1_out0), .out1(decoder_1_out1), .out2(decoder_1_out2), .out3(decoder_1_out3),
    .sel(LX0[1:0]), .en(CX0));
  Decoder #(.select(2), .disabled(0)) decoder_2 (
    .out0(decoder_2_out0), .out1(decoder_2_out1), .out2(decoder_2_out2), .out3(decoder_2_out3), .sel(LX1[1:0]));  // open: en
  Decoder #(.select(2), .disabled(0)) decoder_3 (
    .out0(decoder_3_out0), .out1(decoder_3_out1), .out2(decoder_3_out2), .out3(decoder_3_out3), .sel(LX2[1:0]));  // open: en
  _4regs u_4regs_1 (
    .esto(decoder_1_out0), .datain(X0), .select(LX0[3:2]), .control1(decoder_2_out0), .A1(LX1[3:2]),
    .control2(decoder_3_out0), .A2(LX2[3:2]), .in_5(ck), .in_6(reset), .out1(X1), .out2(X2));
  _4regs u_4regs_2 (
    .esto(decoder_1_out1), .datain(X0), .select(LX0[3:2]), .control1(decoder_2_out1), .A1(LX1[3:2]),
    .control2(decoder_3_out1), .A2(LX2[3:2]), .in_5(ck), .in_6(reset), .out1(X1), .out2(X2));
  // _4regs 4regs_3: pin names not known; wires that end beside it: decoder_1_out2, X0, LX0[3:2], decoder_2_out2, LX1[3:2], decoder_3_out2, LX2[3:2], reset, X1, X2
  // _4regs 4regs_4: pin names not known; wires that end beside it: decoder_1_out3, X0, LX0[3:2], decoder_2_out3, LX1[3:2], decoder_3_out3, LX2[3:2], reset, X1, X2
endmodule
